# Fritzing sketch robotito_bluetooth (saved by Fritzing 0.9.3b)

parts:
  M1 = BTS7960
  Part1 = Arduino Nano (Rev3.0)
  U1 = LIPO-2000mAh [package=lipo-2000]
  MotorA = DC Motor
  U4 = L298_BRIDGE_DRIVER [package=powerso20]
  MotorB = DC Motor
  U3 = LIPO-2000mAh [package=lipo-2000]
  BT1 = Bluetooth HC-06u [package=THT]
  S1 = SPST Switch [package=switch-spdt]
  S2 = SPST Switch [package=switch-spdt]
  Weapon = DC Motor
  Fan = Fan - Ventilador [package=THT]

nets:
  N1: M1.pin1, Part1.D10
  N2: M1.pin2, Part1.D9
  N3: M1.pin3, Part1.D7
  N4: M1.pin4, Part1.D8
  N5: M1.pin7, Part1.5V
  GND: M1.pin8, Part1.GND, U4.GND, U3.-, BT1.GND
  N6: M1.pin9, Weapon.pin_1
  N7: M1.pin10, Weapon.pin_2
  N8: M1.pin11, S2.S, Fan.5V
  N9: M1.pin12, U1.-, Fan.GND
  N10: Part1.D2, U4.IN1
  N11: Part1.D3, U4.ENA
  N12: Part1.D4, U4.IN2
  N13: Part1.D5, BT1.RXD
  N14: Part1.D6, BT1.TXD
  N15: Part1.D11/MOSI, U4.ENB
  N16: Part1.D12/MISO, U4.IN4
  VIN: Part1.VIN, U4.VSS
  3V3: Part1.3V3, BT1.VCC
  N17: Part1.D13/SCK, U4.IN3
  N18: U1.+, S2.P
  N19: MotorA.pin_1, U4.OUT2
  N20: MotorA.pin_2, U4.OUT1
  N21: U4.VS, S1.O
  N22: U4.OUT3, MotorB.pin_1
  N23: U4.OUT4, MotorB.pin_2
  N24: U3.+, S1.P

custom parts:
  BTS7960: BTS7960 43A Peak Power H-Bridge PWM Motor Driver
  Bluetooth HC-06u: Bluetooth HC-06 - face up, pins down 16.5mm x 37.5mm PCB
  Fan - Ventilador: Ventilador de 2 pines, se encuentra comunmente en computadoras de escritorio
